// Logisim project 4BIT ADDER.circ as structural Verilog: 1 circuit, main circuit main
module main (
  input  C0,
  input  A0,
  input  A1,
  input  A2,
  input  A3,
  input  B0,
  input  B1,
  input  B2,
  input  B3,
  output S0,
  output S1,
  output S2,
  output S3,
  output C4
);

  wire full_adder_1_c_2, full_adder_2_c_2, full_adder_3_c_2;

  FULL_ADDER full_adder_1 (.in_1(A0), .in_2(B0), .c(C0), .S(S0), .C_2(full_adder_1_c_2));
  FULL_ADDER full_adder_2 (.in_1(A1), .in_2(B1), .c(full_adder_1_c_2), .S(S1), .C_2(full_adder_2_c_2));
  FULL_ADDER full_adder_3 (.in_1(A2), .in_2(B2), .c(full_adder_2_c_2), .S(S2), .C_2(full_adder_3_c_2));
  FULL_ADDER full_adder_4 (.in_1(A3), .in_2(B3), .c(full_adder_3_c_2), .S(S3), .C_2(C4));
endmodule
