// Logisim project 4bit mult comp.circ as structural Verilog: 1 circuit, main circuit main
module main (
  input  s1,
  input  s2,
  input  A0,
  input  A1,
  input  A2,
  input  A3,
  input  B0,
  input  B1,
  input  B2,
  input  B3,
  output S0,
  output s1_2,
  output s2_2,
  output s3,
  output s4,
  output s5,
  output s6,
  output s7,
  output sign
);

  wire a0b1_out, a0b2_out, a0b3_out, a1b0_out, a1b1_out, a1b2_out, a1b3_out, a2b0_out, a2b1_out, a2b2_out,
       a2b3_out, a3b0_out, a3b1_out, a3b2_out, a3b3_out, main_1_c4, main_1_s1, main_1_s2, main_1_s3,
       main_2_c4, main_2_s1, main_2_s2, main_2_s3;

  xor xor_1 (sign, s1, s2);
  and a0b0 (S0, A0, B0);
  and a1b0 (a1b0_out, A1, B0);
  and a2b0 (a2b0_out, A2, B0);
  and a3b0 (a3b0_out, A3, B0);
  and a0b2 (a0b2_out, B2, A0);
  and a1b2 (a1b2_out, B2, A1);
  and a2b2 (a2b2_out, A2, B2);
  and a3b2 (a3b2_out, B2, A3);
  and a0b1 (a0b1_out, A0, B1);
  and a1b1 (a1b1_out, A1, B1);
  and a2b1 (a2b1_out, A2, B1);
  and a3b1 (a3b1_out, A3, B1);
  and a3b3 (a3b3_out, B3, A3);
  _4BIT_ADDER_main main_1 (
    .C0(1'b0), .A0(a1b0_out), .A1(a2b0_out), .A2(a3b0_out), .A3(1'b0), .B0(a0b1_out), .B1(a1b1_out),
    .B2(a2b1_out), .B3(a3b1_out), .S0(s1_2), .S1(main_1_s1), .S2(main_1_s2), .S3(main_1_s3), .C4(main_1_c4));
  and a0b3 (a0b3_out, B3, A0);
  and a1b3 (a1b3_out, B3, A1);
  and a2b3 (a2b3_out, A2, B3);
  _4BIT_ADDER_main main_2 (
    .C0(1'b0), .A0(main_1_s1), .A1(main_1_s2), .A2(main_1_s3), .A3(main_1_c4), .B0(a0b2_out), .B1(a1b2_out),
    .B2(a2b2_out), .B3(a3b2_out), .S0(s2_2), .S1(main_2_s1), .S2(main_2_s2), .S3(main_2_s3), .C4(main_2_c4));
  _4BIT_ADDER_main main_3 (
    .C0(1'b0), .A0(main_2_s1), .A1(main_2_s2), .A2(main_2_s3), .A3(main_2_c4), .B0(a0b3_out), .B1(a1b3_out),
    .B2(a2b3_out), .B3(a3b3_out), .S0(s3), .S1(s4), .S2(s5), .S3(s6), .C4(s7));
endmodule
