// Logisim project ADD-SUB MULT selector.circ as structural Verilog: 1 circuit, main circuit main
module main (
  input  in_1,
  input  in_2,
  input  in_3,
  input  in_4,
  input  in_5,
  input  in_6,
  input  in_7,
  input  in_8,
  input  in_9,
  input  in_10,
  input  in_11,
  input  in_12,
  output out_13,
  output out_14,
  output out_15,
  output out_16,
  output out_17,
  output out_18
);

  or or_1 (out_13, in_1, in_7);
  or or_2 (out_14, in_2, in_8);
  or or_3 (out_15, in_3, in_9);
  or or_4 (out_16, in_4, in_10);
  or or_5 (out_17, in_5, in_11);
  or or_6 (out_18, in_6, in_12);
endmodule
