// Logisim project ADDSBT selector.circ as structural Verilog: 1 circuit, main circuit main
module main (
  input  in_1,
  input  in_2,
  input  in_3,
  input  in_4,
  input  in_5,
  input  in_6,
  input  in_7,
  output out_8,
  output out_9,
  output out_10,
  output out_11,
  output out_12,
  output out_13
);

  and and_1 (out_8, in_2, in_1);
  and and_2 (out_9, in_3, in_1);
  and and_3 (out_10, in_4, in_1);
  and and_4 (out_11, in_5, in_1);
  and and_5 (out_12, in_6, in_1);
  and and_6 (out_13, in_7, in_1);
endmodule
