// Logisim project ADIITIONANDSUB.circ as structural Verilog: 1 circuit, main circuit main
module main (
  input  A3,
  input  A2,
  input  A1,
  input  A0,
  input  B3,
  input  B2,
  input  B1,
  input  B0,
  input  M,
  input  N,
  output C4,
  output S3,
  output S2,
  output S1,
  output S0
);

  wire and_1_out, and_3_out, main_1_c4, main_1_s0, main_1_s1, main_1_s2, main_1_s3, not_1_out, not_2_out,
       not_3_out, xor_1_out, xor_5_out, xor_6_out, xor_8_out, xor_9_out;

  and and_1 (and_1_out, not_1_out, not_2_out);
  and and_2 (C4, and_1_out, xor_1_out);
  not not_1 (not_1_out, M);
  not not_2 (not_2_out, N);
  xor xor_1 (xor_1_out, N, main_1_c4);
  xor xor_2 (S2, main_1_s2, N);
  xor xor_3 (S3, main_1_s3, N);
  xor xor_4 (S1, main_1_s1, N);
  xor xor_5 (xor_5_out, M, B3);
  xor xor_6 (xor_6_out, M, B2);
  _4BIT_ADDER_main main_1 (
    .C0(and_3_out), .A0(xor_9_out), .A1(xor_8_out), .A2(xor_6_out), .A3(xor_5_out), .B0(A0), .B1(A1),
    .B2(A2), .B3(A3), .S0(main_1_s0), .S1(main_1_s1), .S2(main_1_s2), .S3(main_1_s3), .C4(main_1_c4));
  xor xor_7 (S0, main_1_s0, N);
  xor xor_8 (xor_8_out, M, B1);
  and and_3 (and_3_out, M, not_3_out);
  xor xor_9 (xor_9_out, M, B0);
  not not_3 (not_3_out, N);
endmodule
