// Logisim project BINARY TO BCD.circ as structural Verilog: 1 circuit, main circuit main
module main (
  input  A7,
  input  A6,
  input  A5,
  input  A4,
  input  A3,
  input  A2,
  input  A1,
  input  A0,
  output out_9,
  output out_10,
  output S9,
  output S8,
  output S7,
  output S6,
  output S5,
  output S4,
  output S3,
  output S2,
  output S1,
  output S0
);

  wire main_1_s0, main_1_s1, main_1_s2, main_3_s0, main_3_s1, main_3_s2, main_3_s3, main_4_s0, main_4_s1,
       main_4_s2, main_4_s3, main_5_s0, main_5_s1, main_5_s2, main_5_s3, main_6_s0, main_6_s1, main_6_s2,
       main_6_s3;

  ABIT_ADDTO3_main main_1 (
    .A0(main_5_s3), .A1(main_4_s3), .A2(main_3_s3), .A3(1'b0), .S0(main_1_s0), .S1(main_1_s1),
    .S2(main_1_s2), .S3(S9));
  ABIT_ADDTO3_main main_2 (
    .A0(main_6_s3), .A1(main_1_s0), .A2(main_1_s1), .A3(main_1_s2), .S0(S5), .S1(S6), .S2(S7), .S3(S8));
  ABIT_ADDTO3_main main_3 (
    .A0(A5), .A1(A6), .A2(A7), .A3(1'b0), .S0(main_3_s0), .S1(main_3_s1), .S2(main_3_s2), .S3(main_3_s3));
  ABIT_ADDTO3_main main_4 (
    .A0(A4), .A1(main_3_s0), .A2(main_3_s1), .A3(main_3_s2), .S0(main_4_s0), .S1(main_4_s1), .S2(main_4_s2),
    .S3(main_4_s3));
  ABIT_ADDTO3_main main_5 (
    .A0(A3), .A1(main_4_s0), .A2(main_4_s1), .A3(main_4_s2), .S0(main_5_s0), .S1(main_5_s1), .S2(main_5_s2),
    .S3(main_5_s3));
  ABIT_ADDTO3_main main_6 (
    .A0(A2), .A1(main_5_s0), .A2(main_5_s1), .A3(main_5_s2), .S0(main_6_s0), .S1(main_6_s1), .S2(main_6_s2),
    .S3(main_6_s3));
  ABIT_ADDTO3_main main_7 (.A0(A1), .A1(main_6_s0), .A2(main_6_s1), .A3(main_6_s2), .S0(S1), .S1(S2), .S2(S3), .S3(S4));

  assign out_9 = 1'b0;
  assign out_10 = 1'b0;
  assign S0 = A0;
endmodule
