// Logisim project FINALADD,SUBB0.circ as structural Verilog
module main (
  input  OP,
  input  A0,
  input  A1,
  input  A2,
  input  A3,
  input  A4,
  input  B0,
  input  B1,
  input  B2,
  input  B3,
  input  B4,
  output S0,
  output S1,
  output S2,
  output S3,
  output S4,
  output SIGN
);

  wire and_1_out, COMP_a_b, COMP_a_b_2, COMP_a_b_3, not_1_out, or_1_out, ROP_m, ROP_x;

  comp_main COMP (
    .A3(A3), .B3(B3), .A2(A2), .B2(B2), .A1(A1), .B1(B1), .A0(A0), .B0(B0), .A_B(COMP_a_b),
    .A_B_2(COMP_a_b_2), .A_B_3(COMP_a_b_3));
  real_operator_and_sign_main ROP (.OP(OP), .C(and_1_out), .A4(A4), .B4(B4), .M(ROP_m), .S(SIGN), .X(ROP_x));
  not not_1 (not_1_out, COMP_a_b);
  or or_1 (or_1_out, COMP_a_b_2, COMP_a_b_3);
  and and_1 (and_1_out, not_1_out, or_1_out);
  ADIITIONANDSUB_main main_1 (
    .A3(A3), .A2(A2), .A1(A1), .A0(A0), .B3(B3), .B2(B2), .B1(B1), .B0(B0), .C4(S4), .S3(S3), .S2(S2),
    .S1(S1), .S0(S0), .M(ROP_m), .N(ROP_x));
endmodule
