// Logisim project FULL ADDER.circ as structural Verilog: 1 circuit, main circuit FULL ADDER
module FULL_ADDER (
  input  in_1,
  input  in_2,
  input  c,
  output S,
  output C_2
);

  wire main_1_c, main_1_s, main_2_c;

  half_adder_main main_1 (.x(in_1), .y(in_2), .s(main_1_s), .c(main_1_c));
  half_adder_main main_2 (.x(main_1_s), .y(c), .s(S), .c(main_2_c));
  or or_1 (C_2, main_2_c, main_1_c);
endmodule
