// Logisim project MULT selector.circ as structural Verilog: 1 circuit, main circuit main
module main (
  input  in_1,
  input  in_2,
  input  in_3,
  input  in_4,
  input  in_5,
  input  in_6,
  input  in_7,
  input  in_8,
  input  in_9,
  input  in_10,
  output out_11,
  output out_12,
  output out_13,
  output out_14,
  output out_15,
  output out_16,
  output out_17,
  output out_18,
  output out_19
);

  and and_1 (out_11, in_2, in_1);
  and and_2 (out_12, in_3, in_1);
  and and_3 (out_13, in_4, in_1);
  and and_4 (out_14, in_5, in_1);
  and and_5 (out_15, in_6, in_1);
  and and_6 (out_16, in_7, in_1);
  and and_7 (out_17, in_8, in_1);
  and and_8 (out_18, in_9, in_1);
  and and_9 (out_19, in_10, in_1);
endmodule
