// Logisim project PROJ1.circ as structural Verilog: 1 circuit, main circuit main
module main (
  input  OP,
  input  C,
  input  A3,
  input  A2,
  input  A1,
  input  A0,
  input  B3,
  input  B2,
  input  B1,
  input  B0,
  input  A4,
  input  B4,
  output S4,
  output S3,
  output S2,
  output S1,
  output S0
);

  wire main_1_m, main_1_s, main_1_x;

  real_operator_and_sign_main main_1 (.OP(OP), .C(C), .A4(A4), .B4(B4), .M(main_1_m), .S(main_1_s), .X(main_1_x));
  ADIITIONANDSUB_main main_2 (
    .A3(A3), .A2(A2), .A1(A1), .A0(A0), .B3(B3), .B2(B2), .B1(B1), .B0(B0), .C4(S4), .S3(S3), .S2(S2),
    .S1(S1), .S0(S0), .M(main_1_m), .N(main_1_x));
endmodule
