// Logisim project FINAL PROJECT.circ as structural Verilog: 1 circuit, main circuit main
module main (
  input  A0,
  input  in_2,
  input  in_3,
  input  A1,
  input  A2,
  input  A3,
  input  A4,
  input  B0,
  input  B1,
  input  B2,
  input  B3,
  input  B4
);

  wire main_1_s0, main_1_s1, main_1_s2, main_1_s3, main_1_s4, main_1_sign, main_2_s0, main_2_s1_2,
       main_2_s2_2, main_2_s3, main_2_s4, main_2_s5, main_2_s6, main_2_s7, main_2_sign, main_3_out_8,
       main_3_out_9, main_3_out_10, main_3_out_11, main_3_out_12, main_3_out_13, main_4_out_11,
       main_4_out_12, main_4_out_13, main_4_out_14, main_4_out_15, main_4_out_16, main_4_out_17,
       main_4_out_18, main_4_out_19, main_5_out_13, main_5_out_14, main_5_out_15, main_5_out_16,
       main_5_out_17, main_5_out_18, main_6_out_9, main_6_out_10, main_6_s0, main_6_s1, main_6_s2, main_6_s3,
       main_6_s4, main_6_s5, main_6_s6, main_6_s7, main_6_s8, main_6_s9, main_7_a_2, main_7_b_2, main_7_c_2,
       main_7_d_2, main_7_e, main_7_f, main_7_g, main_8_a_2, main_8_b_2, main_8_c_2, main_8_d_2, main_8_e,
       main_8_f, main_8_g, main_9_a_2, main_9_b_2, main_9_c_2, main_9_d_2, main_9_e, main_9_f, main_9_g,
       xnor_1_out, xor_1_out;

  FINALADD_SUBB0_main main_1 (
    .A0(A0), .A1(A1), .A2(A2), .A3(A3), .A4(A4), .B0(B0), .B1(B1), .B2(B2), .B3(B3), .B4(B4), .OP(in_2),
    .S0(main_1_s0), .S1(main_1_s1), .S2(main_1_s2), .S3(main_1_s3), .S4(main_1_s4), .SIGN(main_1_sign));
  _4bit_mult_comp_main main_2 (
    .s1(A4), .s2(B4), .A0(A0), .A1(A1), .A2(A2), .A3(A3), .B0(B0), .B1(B1), .B2(B2), .B3(B3), .S0(main_2_s0),
    .s1_2(main_2_s1_2), .s2_2(main_2_s2_2), .s3(main_2_s3), .s4(main_2_s4), .s5(main_2_s5), .s6(main_2_s6),
    .s7(main_2_s7), .sign(main_2_sign));
  xor xor_1 (xor_1_out, in_3, in_2);
  xnor xnor_1 (xnor_1_out, in_3, in_2);
  ADDSBT_selector_main main_3 (
    .in_1(xnor_1_out), .in_2(main_1_s0), .in_3(main_1_s1), .in_4(main_1_s2), .in_5(main_1_s3),
    .in_6(main_1_s4), .in_7(main_1_sign), .out_8(main_3_out_8), .out_9(main_3_out_9), .out_10(main_3_out_10),
    .out_11(main_3_out_11), .out_12(main_3_out_12), .out_13(main_3_out_13));
  MULT_selector_main main_4 (
    .in_1(xor_1_out), .in_2(main_2_s0), .in_3(main_2_s1_2), .in_4(main_2_s2_2), .in_5(main_2_s3),
    .in_6(main_2_s4), .in_7(main_2_s5), .in_8(main_2_s6), .in_9(main_2_s7), .in_10(main_2_sign),
    .out_11(main_4_out_11), .out_12(main_4_out_12), .out_13(main_4_out_13), .out_14(main_4_out_14),
    .out_15(main_4_out_15), .out_16(main_4_out_16), .out_17(main_4_out_17), .out_18(main_4_out_18),
    .out_19(main_4_out_19));
  ADD_SUB_MULT_selector_main main_5 (
    .in_1(main_3_out_8), .in_2(main_3_out_9), .in_3(main_3_out_10), .in_4(main_3_out_11),
    .in_5(main_3_out_12), .in_6(main_3_out_13), .in_7(main_4_out_11), .in_8(main_4_out_12),
    .in_9(main_4_out_13), .in_10(main_4_out_14), .in_11(main_4_out_15), .in_12(main_4_out_19),
    .out_13(main_5_out_13), .out_14(main_5_out_14), .out_15(main_5_out_15), .out_16(main_5_out_16),
    .out_17(main_5_out_17), .out_18(main_5_out_18));
  BINARY_TO_BCD_main main_6 (
    .A7(main_4_out_18), .A6(main_4_out_17), .A5(main_4_out_16), .A4(main_5_out_17), .A3(main_5_out_16),
    .A2(main_5_out_15), .A1(main_5_out_14), .A0(main_5_out_13), .out_9(main_6_out_9), .out_10(main_6_out_10),
    .S9(main_6_s9), .S8(main_6_s8), .S7(main_6_s7), .S6(main_6_s6), .S5(main_6_s5), .S4(main_6_s4),
    .S3(main_6_s3), .S2(main_6_s2), .S1(main_6_s1), .S0(main_6_s0));
  _7_segments_main main_7 (
    .D(main_6_s0), .C(main_6_s1), .B(main_6_s2), .A(main_6_s3), .a_2(main_7_a_2), .b_2(main_7_b_2),
    .c_2(main_7_c_2), .d_2(main_7_d_2), .e(main_7_e), .f(main_7_f), .g(main_7_g));
  _7_segments_main main_8 (
    .D(main_6_s4), .C(main_6_s5), .B(main_6_s6), .A(main_6_s7), .a_2(main_8_a_2), .b_2(main_8_b_2),
    .c_2(main_8_c_2), .d_2(main_8_d_2), .e(main_8_e), .f(main_8_f), .g(main_8_g));
  _7_segments_main main_9 (
    .D(main_6_s8), .C(main_6_s9), .B(main_6_out_10), .A(main_6_out_9), .a_2(main_9_a_2), .b_2(main_9_b_2),
    .c_2(main_9_c_2), .d_2(main_9_d_2), .e(main_9_e), .f(main_9_f), .g(main_9_g));
  _7_Segment_Display u_7_segment_display_1 (
    .g(main_7_g), .f(main_7_f), .a(main_7_a_2), .b(main_7_b_2), .e(main_7_e), .d(main_7_d_2), .c(main_7_c_2));  // open: dp
  _7_Segment_Display u_7_segment_display_2 (
    .g(main_8_g), .f(main_8_f), .a(main_8_a_2), .b(main_8_b_2), .e(main_8_e), .d(main_8_d_2), .c(main_8_c_2));  // open: dp
  _7_Segment_Display u_7_segment_display_3 (
    .g(main_9_g), .f(main_9_f), .a(main_9_a_2), .b(main_9_b_2), .e(main_9_e), .d(main_9_d_2), .c(main_9_c_2));  // open: dp

  // Notes on the sheet:
  //   Case 1,1 ->addition
  //   Case 0,0->subtraction
  //   Case 1,0 or 0,1 ->Multiplication
  //   sign
endmodule
