// Logisim project hehe.circ as structural Verilog: 1 circuit, main circuit main
module main (
  input  in_1,
  input  in_2,
  input  in_3,
  input  in_4,
  input  in_5,
  input  in_6,
  input  in_7,
  input  in_8,
  input  in_9,
  input  in_10,
  input  in_11,
  input  in_12,
  input  in_13
);

  wire main_1_s0, main_1_s1, main_1_s2, main_1_s3, main_1_s4, main_1_sign, xnor_1_out;

  FINALADD_SUBB0_main main_1 (
    .A0(in_1), .A1(in_3), .A2(in_4), .A3(in_5), .A4(in_6), .B0(in_7), .B1(in_8), .B2(in_9), .B3(in_10),
    .B4(in_11), .OP(in_2), .S0(main_1_s0), .S1(main_1_s1), .S2(main_1_s2), .S3(main_1_s3), .S4(main_1_s4),
    .SIGN(main_1_sign));
  xnor xnor_1 (xnor_1_out, in_12, in_13);
  // AND_Gate and_1 has open pins: in0=main_1_s0, in1=xnor_1_out, out=open
  // AND_Gate and_2 has open pins: in0=main_1_s1, in1=xnor_1_out, out=open
  // AND_Gate and_3 has open pins: in0=main_1_s2, in1=xnor_1_out, out=open
  // AND_Gate and_4 has open pins: in0=main_1_s3, in1=xnor_1_out, out=open
  // AND_Gate and_5 has open pins: in0=main_1_s4, in1=xnor_1_out, out=open
endmodule
