// Logisim project real operator and sign.circ as structural Verilog: 1 circuit, main circuit main
module main (
  input  OP,
  input  C,
  input  A4,
  input  B4,
  output M,
  output S,
  output X
);

  wire and_1_out, and_2_out, and_3_out, and_4_out, and_5_out, and_6_out, and_7_out, and_8_out, and_9_out,
       and_10_out, and_11_out, not_1_out, not_2_out, not_3_out, not_4_out, not_5_out, not_6_out, not_7_out,
       not_8_out, not_9_out, not_10_out, not_11_out, not_12_out, not_13_out, not_14_out, not_15_out,
       not_16_out, not_17_out, not_18_out, not_19_out, not_20_out;

  not not_1 (not_1_out, OP);
  and and_1 (and_1_out, not_1_out, not_2_out, B4);
  not not_2 (not_2_out, A4);
  not not_3 (not_3_out, OP);
  and and_2 (and_2_out, not_3_out, A4, not_4_out);
  not not_4 (not_4_out, B4);
  not not_5 (not_5_out, A4);
  and and_3 (and_3_out, OP, not_5_out, not_6_out);
  not not_6 (not_6_out, B4);
  and and_4 (and_4_out, OP, A4, B4);
  not not_7 (not_7_out, OP);
  and and_5 (and_5_out, not_7_out, not_8_out, B4);
  not not_8 (not_8_out, C);
  and and_6 (and_6_out, C, A4);
  not not_9 (not_9_out, C);
  and and_7 (and_7_out, OP, not_9_out, not_10_out);
  not not_10 (not_10_out, B4);
  not not_11 (not_11_out, OP);
  not not_12 (not_12_out, C);
  not not_13 (not_13_out, A4);
  not not_14 (not_14_out, OP);
  not not_15 (not_15_out, C);
  not not_16 (not_16_out, B4);
  not not_17 (not_17_out, C);
  not not_18 (not_18_out, A4);
  not not_19 (not_19_out, B4);
  not not_20 (not_20_out, C);
  or or_1 (M, and_1_out, and_2_out, and_3_out, and_4_out);
  or or_2 (S, and_5_out, and_6_out, and_7_out);
  and and_8 (and_8_out, not_11_out, not_12_out, not_13_out, B4);
  and and_9 (and_9_out, not_14_out, not_15_out, A4, not_16_out);
  and and_10 (and_10_out, OP, not_17_out, not_18_out, not_19_out);
  and and_11 (and_11_out, OP, not_20_out, A4, B4);
  or or_3 (X, and_8_out, and_9_out, and_10_out, and_11_out);
endmodule
